// Logisim project 10dop.circ as structural Verilog: 1 circuit, main circuit main
module main (
  input  not_R,
  input  J,
  input  not_C,
  input  K,
  input  not_S,
  input  not_S_2,
  input  not_S_3,
  input  J_2,
  input  J_3,
  input  C,
  input  C_2,
  input  K_2,
  input  K_3,
  input  not_R_2,
  input  not_R_3
);

  wire nand_8_out, nor_1_out, nor_2_out, nor_3_out, nor_4_out, nor_5_out, nor_6_out, nor_7_out, nor_8_out,
       nor_9_out, nor_10_out;

  nor nor_1 (nor_1_out, not_R, not_R);
  nor nor_2 (nor_2_out, not_S, not_S);
  nor nor_3 (nor_3_out, nor_10_out, J, not_C);
  nor nor_4 (nor_4_out, not_C, K, nor_9_out);
  nor nor_5 (nor_5_out, nor_1_out, nor_3_out, nor_6_out);
  nor nor_6 (nor_6_out, nor_5_out, nor_4_out, nor_2_out);
  nor nor_7 (nor_7_out, nor_5_out, nor_3_out, nor_4_out);
  nor nor_8 (nor_8_out, nor_4_out, nor_3_out, nor_6_out);
  nor nor_9 (nor_9_out, nor_1_out, nor_10_out, nor_7_out);
  nor nor_10 (nor_10_out, nor_8_out, nor_9_out, nor_2_out);
  LED Q (.in(nor_9_out));
  LED not_Q (.in(nor_10_out));
  nand nand_1 (not_R_2, not_R_2, J_2, C);
  nand nand_2 (not_R_2, J_2, C, C);
  nand nand_3 (not_R_2, C, C, K_3);
  nand nand_4 (not_R_2, C, K_3, not_R_2);
  nand nand_5 (not_R_2, not_R_2, not_R_2, not_R_2);
  nand nand_6 (not_R_2, not_R_2, not_R_2, nand_8_out);
  nand nand_7 (not_R_2, not_R_2, not_R_2, not_R_2);
  nand nand_8 (nand_8_out, not_R_2, not_R_2, not_R_3);
  nand nand_9 (J_2, not_R_2, not_R_2, not_R_2);
  nand nand_10 (not_R_2, not_R_2, not_R_2, not_R_2);
  nand nand_11 (K_3, not_R_2, not_R_2, not_R_2);
  nand nand_12 (K_3, not_R_2, not_R_2, nand_8_out);
  nand nand_13 (K_3, not_R_2, not_R_2, J_2);
  LED Q_2 (.in(K_3));
  nand nand_14 (not_R_2, not_R_2, J_2, not_R_2);
  nand nand_15 (not_R_2, K_3, K_3, not_R_2);
  LED not_Q_2 (.in(not_R_2));
  nand nand_16 (J_2, K_3, not_R_2, not_R_3);
  LED Q_3 (.in(not_R_2));
  LED not_Q_3 (.in(J_2));

  assign C_2 = C;
  assign J_3 = C;
  assign K_2 = C;
  assign not_S_2 = not_R_2;
  assign not_S_3 = not_R_2;

  // Notes on the sheet:
  //   Триггер 1.9
  //   Триггер 1.9
  //   JK-триггер, выполненный по схеме без инвертора
  //   JK-триггер, выполненный по схеме без инвертора
endmodule
