// Logisim project 9dop.circ as structural Verilog: 1 circuit, main circuit main
module main (
  input  in_1,
  input  in_2,
  input  in_3,
  input  in_4
);

  wire decoder_1_out0, decoder_1_out1, decoder_1_out2, decoder_1_out3, decoder_1_out4, decoder_1_out5,
       decoder_1_out6, decoder_1_out7, decoder_1_out8, decoder_1_out9, decoder_1_out10, decoder_1_out11,
       decoder_1_out12, decoder_1_out13, decoder_1_out14, decoder_1_out15, or_1_out, or_2_out, or_3_out,
       or_4_out, or_5_out, or_6_out, or_7_out, or_8_out, or_9_out, or_10_out, or_11_out, or_12_out;
  wire [3:0] priority_encoder_1_out, priority_encoder_2_out;

  Decoder #(.select(4)) decoder_1 (
    .out0(decoder_1_out0), .out1(decoder_1_out1), .out2(decoder_1_out2), .out3(decoder_1_out3),
    .out4(decoder_1_out4), .out5(decoder_1_out5), .out6(decoder_1_out6), .out7(decoder_1_out7),
    .out8(decoder_1_out8), .out9(decoder_1_out9), .out10(decoder_1_out10), .out11(decoder_1_out11),
    .out12(decoder_1_out12), .out13(decoder_1_out13), .out14(decoder_1_out14), .out15(decoder_1_out15),
    .sel({in_1, in_2, in_3, in_4}));  // open: en
  or or_1 (or_1_out, decoder_1_out0, decoder_1_out1, decoder_1_out2, decoder_1_out3, decoder_1_out4, decoder_1_out5, decoder_1_out6, decoder_1_out7, decoder_1_out8, decoder_1_out9);
  or or_2 (or_2_out, decoder_1_out11, decoder_1_out12, decoder_1_out13, decoder_1_out14, decoder_1_out15);
  Priority_Encoder #(.select(4)) priority_encoder_1 (
    .in0(or_1_out), .in1(or_2_out), .out(priority_encoder_1_out));  // open: in2, in3, in4, in5, in6, in7, in8, in9, in10, in11, in12, in13, in14, in15, gs, en_out, en_in
  Hex_Digit_Display hex_digit_display_1 (.value(priority_encoder_1_out));  // open: dp
  or or_3 (or_3_out, decoder_1_out0, decoder_1_out11);
  or or_4 (or_4_out, decoder_1_out1, decoder_1_out12);
  or or_5 (or_5_out, decoder_1_out3, decoder_1_out14);
  or or_6 (or_6_out, decoder_1_out2, decoder_1_out13);
  or or_7 (or_7_out, decoder_1_out4, decoder_1_out15);
  buf or_8 (or_8_out, decoder_1_out5);  // OR_Gate
  buf or_9 (or_9_out, decoder_1_out6);  // OR_Gate
  buf or_10 (or_10_out, decoder_1_out7);  // OR_Gate
  buf or_11 (or_11_out, decoder_1_out8);  // OR_Gate
  buf or_12 (or_12_out, decoder_1_out9);  // OR_Gate
  Priority_Encoder #(.select(4)) priority_encoder_2 (
    .in0(or_3_out), .in1(or_4_out), .in2(or_6_out), .in3(or_5_out), .in4(or_7_out), .in5(or_8_out),
    .in6(or_9_out), .in7(or_10_out), .in8(or_11_out), .in9(or_12_out), .in10(decoder_1_out10),
    .out(priority_encoder_2_out));  // open: in11, in12, in13, in14, in15, gs, en_out, en_in
  Hex_Digit_Display hex_digit_display_2 (.value(priority_encoder_2_out));  // open: dp
endmodule
